# Fritzing sketch IntelliRoom (saved by Fritzing 0.9.1b)
circuit board: 10.0578cm x 5.49187cm
breadboards: 1

parts:
  arduino = Arduino Uno (Rev3)
  Q1 = NPN-Transistor [package="TO92 [THT]"]
  Q2 = NPN-Transistor [package="TO92 [THT]"]
  pirLedStrip = LEDs [package=led10mm]
  timeLedStrip = LEDs [package=led10mm]
  12v_power_plug = Power plug
  pir = LHi958 [package=to-39]
  S1 = Square Pushbutton

nets:
  N1: arduino.D8, pir.S
  N2: arduino.D9_PWM, Q2.E
  N3: arduino.D10_PWM/SS, Q1.E
  N4: arduino.D2, S1.leg0
  N5: arduino.5V, pir.D
  GND: arduino.GND, Q1.B, Q2.B, 12v_power_plug.GND, pir.GND, S1.leg1
  VIN: arduino.VIN, pirLedStrip.A, timeLedStrip.A, 12v_power_plug.VCC
  N6: Q1.C, pirLedStrip.C
  N7: Q2.C, timeLedStrip.C
